# Fritzing sketch shema (saved by Fritzing 0.9.3b)
breadboards: 1

parts:
  Button = Pushbutton [package="[SMD]"]
  Potentiometer = Rotary Potentiometer (Small) [maximum_resistance=100kΩ package=THT]
  RGB_LED = RGB LED (com. cathode, rgb) [package="5 mm [THT]"]
  Composant1 = Arduino Uno (Rev3)

nets:
  N1: Button.Pin_1, Button.Pin_2, Potentiometer.leg2, Composant1.5V
  N2: Button.Pin_3, Button.Pin_4, Composant1.D13/SCK
  N3: Potentiometer.leg1, RGB_LED.common_cathode, Composant1.GND
  N4: Potentiometer.wiper, Composant1.A0
  N5: RGB_LED.red_anode, Composant1.D3_PWM
  N6: RGB_LED.green_anode, Composant1.D5_PWM
  N7: RGB_LED.blue_anode, Composant1.D6_PWM
